# Fritzing sketch block diagram (saved by Fritzing 1.0.2b)
breadboards: 1

parts:
  Součástka1 = Arduino Nano (Rev3.0)
  Součástka2 = NRF24L01+ Breakout Board
  R1 = Rotary Potentiometer (Large) [maximum_resistance=100kΩ knob_status=50% power=0.5W package=THT]
  S1 = Pushbutton [package="[THT]"]
  Součástka3 = BH1750
  LED1 = RGB LED - (4 legs) [color="Red (633nm)" current=0.030A package="5 mm [THT]"]

nets:
  GND: Součástka1.GND, Součástka2.GND, R1.leg2, S1.Pin_1, S1.Pin_2, Součástka3.connector9, LED1.red_cathode
  N1: Součástka1.D2, LED1.common_anode
  N2: Součástka1.D3, LED1.green_cathode
  N3: Součástka1.D4, LED1.blue_cathode
  N4: Součástka1.D5, S1.Pin_3, S1.Pin_4
  N5: Součástka1.D7, Součástka2.CE
  N6: Součástka1.D8, Součástka2.CS
  N7: Součástka1.D11/MOSI, Součástka2.MOSI
  N8: Součástka1.D12/MISO, Součástka2.MISO
  N9: Součástka1.5V, R1.leg1, Součástka3.connector8
  N10: Součástka1.A5, Součástka3.connector10
  N11: Součástka1.A4, Součástka3.connector12
  N12: Součástka1.A0, R1.wiper
  3V3: Součástka1.3V3, Součástka2.VCC
  N13: Součástka1.D13/SCK, Součástka2.SCK
